# Fritzing sketch Schematic diagram (saved by Fritzing 0.9.6b)
breadboards: 1
perfboards: 1

parts:
  元件1 = Arduino Mega ADK (Rev3)
  元件2 = LQFP-32 [chip_label=daq package=LQFP]
  S1 = Pushbutton [package="[SMD]"]
  R4 = Resistor [tolerance=±5% power=0.25 resistance=220 package=THT]
  R11 = Resistor [tolerance=±5% power=0.25 resistance=220 package=THT]
  S2 = Pushbutton [package="[SMD]"]
  S3 = Pushbutton [package="[SMD]"]
  S4 = Pushbutton [package="[SMD]"]
  S5 = Pushbutton [package="[SMD]"]
  R12 = Resistor [tolerance=±5% power=0.25 resistance=220 package=THT]
  R13 = Resistor [tolerance=±5% power=0.25 resistance=220 package=THT]
  R14 = Resistor [tolerance=±5% power=0.25 resistance=220 package=THT]
  R15 = Resistor [tolerance=±5% power=0.25 resistance=220 package=THT]
  R16 = Resistor [tolerance=±5% power=0.25 resistance=220 package=THT]
  R17 = Resistor [tolerance=±5% power=0.25 resistance=220 package=THT]
  R18 = Resistor [tolerance=±5% power=0.25 resistance=220 package=THT]
  R19 = Resistor [tolerance=±5% power=0.25 resistance=220 package=THT]

nets:
  N1: 元件1.GND, R14.Pin_1
  N2: 元件1.D2_PWM, 元件2.32
  N3: 元件1.D3_PWM, 元件2.31
  N4: 元件1.D4_PWM, 元件2.30
  N5: 元件1.D5_PWM, 元件2.29
  N6: 元件1.D6_PWM, 元件2.28
  N7: 元件1.D7_PWM, 元件2.27
  N8: 元件2.3, S4.Pin_1, S4.Pin_2, R16.Pin_0, R17.Pin_0
  N9: S1.Pin_1, S1.Pin_2, R4.Pin_0, R11.Pin_0
  N10: S1.Pin_3, S1.Pin_4
  N11: R4.Pin_1, R19.Pin_1
  N12: S2.Pin_1, S2.Pin_2, R12.Pin_0, R13.Pin_0
  N13: S2.Pin_3, S2.Pin_4
  N14: S3.Pin_1, S3.Pin_2, R14.Pin_0, R15.Pin_0
  N15: S3.Pin_3, S3.Pin_4
  N16: S4.Pin_3, S4.Pin_4
  N17: S5.Pin_1, S5.Pin_2, R18.Pin_0, R19.Pin_0
  N18: S5.Pin_3, S5.Pin_4

notes:
  五个开关模拟传感器阵列
  这个是数据采集卡的接口设置
